# Fritzing sketch BeachSafety2018 (saved by Fritzing 0.9.3b)

parts:
  Part1 = Arduino Nano (Rev3.0)
  U1 = FS1000A - 433Mhz RF Transmitter [package=THT]
  Part2 = Adafruit FONA 808 Breakout [part_number="Adafruit #2542"]

nets:
  GND: Part1.GND, U1.GND, Part2.GND, Part2.Key
  N1: Part1.D2, Part2.RXD
  N2: Part1.D3, Part2.TXD
  N3: Part1.D4, Part2.Reset
  5V: Part1.5V, U1.VCC, Part2.+5V
  N4: Part1.D13/SCK, U1.DATA

notes:
  https://learn.adafruit.com/adafruit-fona-808-cellular-plus-gps-breakout/wiring-toarduino
  http://www.instructables.com/id/Arduino-433mhz-Wireless-Transmitter-Receiver-SWITC/

custom parts:
  FS1000A - 433Mhz RF Transmitter: This is 433Mhz RF transmitter with receiver kit for Arduino ARM MCU wireless Application environment: Remote control switch, receiver module, motorcycles, automobile anti-theft products, home security products, electric doors, shutter doors, windows, remote control socket, remote control LED, remote audio remote control electric doors, garage door remote control, remote control retractable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
  Adafruit FONA 808 Breakout: Cellular + GPS tracking, all in one? Oh yes! Introducing Adafruit FONA 808 MiniGSM + GPS, an all-in-one cellular phone module with that lets you add location-tracking, voice, text, SMS and data to your project in an adorable little package.
